// Logisim project Lab_2_Solutions.circ as structural Verilog: 20 circuits, main circuit Part_II
module Part_I (
  input  [3:0] SW15_12,
  input  [3:0] SW11_8,
  input  [3:0] SW7_4,
  input  [3:0] SW3_0
);

  wire H00, H01, H02, H03, H04, H05, H06, H07, H10, H11, H12, H13, H14, H15, H16, H17, H20, H21, H22, H23,
       H24, H25, H26, H27, H30, H31, H32, H33, H34, H35, H36, H37;

  _7_Segment_Display #(.decimalPoint("true")) HEX3 (
    .g(H36), .f(H35), .a(H30), .b(H31), .e(H34), .d(H33), .c(H32), .dp(H37));
  BCD_Display bcd_display_1 (.BCD(SW15_12), .SEG({H37, H36, H35, H34, H33, H32, H31, H30}));
  _7_Segment_Display #(.decimalPoint("true")) HEX2 (
    .g(H26), .f(H25), .a(H20), .b(H21), .e(H24), .d(H23), .c(H22), .dp(H27));
  BCD_Display bcd_display_2 (.BCD(SW11_8), .SEG({H27, H26, H25, H24, H23, H22, H21, H20}));
  _7_Segment_Display #(.decimalPoint("true")) HEX1 (
    .g(H16), .f(H15), .a(H10), .b(H11), .e(H14), .d(H13), .c(H12), .dp(H17));
  BCD_Display bcd_display_3 (.BCD(SW7_4), .SEG({H17, H16, H15, H14, H13, H12, H11, H10}));
  _7_Segment_Display #(.decimalPoint("true")) HEX0 (
    .g(H06), .f(H05), .a(H00), .b(H01), .e(H04), .d(H03), .c(H02), .dp(H07));
  BCD_Display bcd_display_4 (.BCD(SW3_0), .SEG({H07, H06, H05, H04, H03, H02, H01, H00}));

  // Other names for the same wires on the sheet: D0[3:0] = SW3_0; D1[3:0] = SW7_4; D2[3:0] = SW11_8;
  //   D3[3:0] = SW15_12; HEX0_SEG[7:0] = {H07, H06, H05, H04, H03, H02, H01, H00};
  //   HEX1_SEG[7:0] = {H17, H16, H15, H14, H13, H12, H11, H10};
  //   HEX2_SEG[7:0] = {H27, H26, H25, H24, H23, H22, H21, H20};
  //   HEX3_SEG[7:0] = {H37, H36, H35, H34, H33, H32, H31, H30}

  // Notes on the sheet:
  //   PART I  |  Four independent decimal displays
  //   Each group of four switches drives its matching display. Digits 0..9 are defined; inputs 10..15 are don't-cares.
  //   HEX3  |  D3
  //   HEX2  |  D2
  //   HEX1  |  D1
  //   HEX0  |  D0
endmodule

module Part_II (
  input  v3,
  input  v2,
  input  v1,
  input  v0
);

  wire circuita_1_o0, circuita_1_o1, circuita_1_o2, d0, d1, d2, d3, d4, d5, d6, multiplexer_1_out,
       multiplexer_2_out, multiplexer_3_out, multiplexer_4_out, s0, s1, s2, s3, s4, s5, s6, z;
  wire [7:0] seg7_decoder_1_o_seg;

  myComparator mycomparator_1 (.v3(v3), .v2(v2), .v1(v1), .v0(v0), .z(z));
  CircuitA circuita_1 (.i2(v2), .i1(v1), .i0(v0), .o2(circuita_1_o2), .o1(circuita_1_o1), .o0(circuita_1_o0));
  Multiplexer multiplexer_1 (.in0(v3), .in1(1'b0), .out(multiplexer_1_out), .sel(z));
  Multiplexer multiplexer_2 (.in0(v2), .in1(circuita_1_o2), .out(multiplexer_2_out), .sel(z));
  Multiplexer multiplexer_3 (.in0(v1), .in1(circuita_1_o1), .out(multiplexer_3_out), .sel(z));
  Multiplexer multiplexer_4 (.in0(v0), .in1(circuita_1_o0), .out(multiplexer_4_out), .sel(z));
  CircuitB circuitb_1 (.z(z), .s6(d6), .s5(d5), .s4(d4), .s3(d3), .s2(d2), .s1(d1), .s0(d0));
  Seg7_Decoder seg7_decoder_1 (
    .i_m3(multiplexer_1_out), .i_m2(multiplexer_2_out), .i_m1(multiplexer_3_out), .i_m0(multiplexer_4_out),
    .o_seg(seg7_decoder_1_o_seg));
  not not_1 (s0, seg7_decoder_1_o_seg[0]);
  not not_2 (s1, seg7_decoder_1_o_seg[1]);
  not not_3 (s2, seg7_decoder_1_o_seg[2]);
  not not_4 (s3, seg7_decoder_1_o_seg[3]);
  not not_5 (s4, seg7_decoder_1_o_seg[4]);
  not not_6 (s5, seg7_decoder_1_o_seg[5]);
  not not_7 (s6, seg7_decoder_1_o_seg[6]);
  _7_Segment_Display u_7_segment_display_1 (.g(d6), .f(d5), .a(d0), .b(d1), .e(d4), .d(d3), .c(d2), .dp(1'b0));
  _7_Segment_Display u_7_segment_display_2 (.g(s6), .f(s5), .a(s0), .b(s1), .e(s4), .d(s3), .c(s2), .dp(1'b0));

  // Notes on the sheet:
  //   PART II  |  Four-bit binary to decimal
  //   Poke v3..v0 to try 0 through 15. Repaired decoder digit 7 and tied m3 mux input 1 to zero.
endmodule

module Part_III (
  input  [3:0] SW7_4,
  input  [3:0] SW3_0,
  input  SW8,
  output [3:0] S,
  output cout
);

  LED LEDR0 (.in(SW3_0[0]));
  LED LEDR1 (.in(SW3_0[1]));
  LED LEDR2 (.in(SW3_0[2]));
  LED LEDR3 (.in(SW3_0[3]));
  LED LEDR4 (.in(SW7_4[0]));
  LED LEDR5 (.in(SW7_4[1]));
  LED LEDR6 (.in(SW7_4[2]));
  LED LEDR7 (.in(SW7_4[3]));
  LED LEDR8 (.in(SW8));
  Ripple_Adder_4 ripple_adder_4_1 (.A(SW7_4), .B(SW3_0), .cin(SW8), .S(S), .cout(cout));
  LED LEDG0 (.in(S[0]));
  LED LEDG1 (.in(S[1]));
  LED LEDG2 (.in(S[2]));
  LED LEDG3 (.in(S[3]));
  LED LEDG4 (.in(cout));

  // Other names for the same wires on the sheet: LEDG[4:0] = {cout, S}; B[3:0] = SW3_0;
  //   LEDR[8:0] = {SW8, SW7_4, SW3_0}; A[3:0] = SW7_4; cin = SW8

  // Notes on the sheet:
  //   PART III  |  Four-bit ripple-carry adder
  //   SW7..4 = A, SW3..0 = B, SW8 = cin. Red LEDs mirror inputs; green LEDs show cout and S.
endmodule

module Part_IV (
  input  [3:0] SW7_4,
  input  [3:0] SW3_0,
  input  SW8,
  output [3:0] S0,
  output [3:0] S1,
  output ERROR
);

  wire C4, H00, H01, H02, H03, H04, H05, H06, H07, H10, H11, H12, H13, H14, H15, H16, H17, H40, H41, H42,
       H43, H44, H45, H46, H47, H60, H61, H62, H63, H64, H65, H66, H67;
  wire [3:0] LEDG;

  _7_Segment_Display #(.decimalPoint("true")) HEX6 (
    .g(H66), .f(H65), .a(H60), .b(H61), .e(H64), .d(H63), .c(H62), .dp(H67));
  BCD_Display bcd_display_1 (.BCD(SW7_4), .SEG({H67, H66, H65, H64, H63, H62, H61, H60}));
  LED LEDR0 (.in(SW3_0[0]));
  LED LEDR1 (.in(SW3_0[1]));
  LED LEDR2 (.in(SW3_0[2]));
  LED LEDR3 (.in(SW3_0[3]));
  LED LEDR4 (.in(SW7_4[0]));
  LED LEDR5 (.in(SW7_4[1]));
  LED LEDR6 (.in(SW7_4[2]));
  LED LEDR7 (.in(SW7_4[3]));
  LED LEDR8 (.in(SW8));
  BCD_Adder_1 bcd_adder_1_1 (.A(SW7_4), .B(SW3_0), .cin(SW8), .S0(S0), .S1(S1[0]), .RAW(LEDG), .C4(C4), .ERROR(ERROR));
  _7_Segment_Display #(.decimalPoint("true")) HEX4 (
    .g(H46), .f(H45), .a(H40), .b(H41), .e(H44), .d(H43), .c(H42), .dp(H47));
  BCD_Display bcd_display_2 (.BCD(SW3_0), .SEG({H47, H46, H45, H44, H43, H42, H41, H40}));
  LED LEDG0 (.in(LEDG[0]));
  LED LEDG1 (.in(LEDG[1]));
  LED LEDG2 (.in(LEDG[2]));
  LED LEDG3 (.in(LEDG[3]));
  LED LEDG4 (.in(C4));
  _7_Segment_Display #(.decimalPoint("true")) HEX1 (
    .g(H16), .f(H15), .a(H10), .b(H11), .e(H14), .d(H13), .c(H12), .dp(H17));
  BCD_Display bcd_display_3 (.BCD({3'b000, S1[0]}), .SEG({H17, H16, H15, H14, H13, H12, H11, H10}));
  LED LEDG8 (.in(ERROR));
  _7_Segment_Display #(.decimalPoint("true")) HEX0 (
    .g(H06), .f(H05), .a(H00), .b(H01), .e(H04), .d(H03), .c(H02), .dp(H07));
  BCD_Display bcd_display_4 (.BCD(S0), .SEG({H07, H06, H05, H04, H03, H02, H01, H00}));

  assign S1[3:1] = 3'b000;

  // Other names for the same wires on the sheet: HEX0_SEG[7:0] = {H07, H06, H05, H04, H03, H02, H01, H00};
  //   HEX1_SEG[7:0] = {H17, H16, H15, H14, H13, H12, H11, H10};
  //   HEX4_SEG[7:0] = {H47, H46, H45, H44, H43, H42, H41, H40};
  //   HEX6_SEG[7:0] = {H67, H66, H65, H64, H63, H62, H61, H60}; RAW[3:0] = LEDG; LEDG[4] = C4; B[3:0] = SW3_0;
  //   LEDR[8:0] = {SW8, SW7_4, SW3_0}; A[3:0] = SW7_4; cin = SW8; carry = S1[0]

  // Notes on the sheet:
  //   PART IV  |  One-digit BCD addition
  //   SW7..4 = A, SW3..0 = B, SW8 = cin. HEX6 + HEX4 + cin = HEX1 HEX0. LEDG8 flags invalid BCD input.
  //   HEX6  |  A
  //   HEX4  |  B
  //   HEX1  |  S1
  //   Valid digits: 0..9
  //   Maximum sum: 9 + 9 + 1 = 19
  //   Invalid BCD input
  //   HEX0  |  S0
endmodule

module Part_V (
  input  [7:0] SW15_8,
  input  [7:0] SW7_0,
  output [3:0] S0,
  output [3:0] S1,
  output [3:0] S2,
  output ERROR
);

  wire H00, H01, H02, H03, H04, H05, H06, H07, H10, H11, H12, H13, H14, H15, H16, H17, H20, H21, H22, H23,
       H24, H25, H26, H27, H40, H41, H42, H43, H44, H45, H46, H47, H50, H51, H52, H53, H54, H55, H56, H57,
       H60, H61, H62, H63, H64, H65, H66, H67, H70, H71, H72, H73, H74, H75, H76, H77;

  _7_Segment_Display #(.decimalPoint("true")) HEX7 (
    .g(H76), .f(H75), .a(H70), .b(H71), .e(H74), .d(H73), .c(H72), .dp(H77));
  BCD_Display bcd_display_1 (.BCD(SW15_8[7:4]), .SEG({H77, H76, H75, H74, H73, H72, H71, H70}));
  _7_Segment_Display #(.decimalPoint("true")) HEX2 (
    .g(H26), .f(H25), .a(H20), .b(H21), .e(H24), .d(H23), .c(H22), .dp(H27));
  _7_Segment_Display #(.decimalPoint("true")) HEX6 (
    .g(H66), .f(H65), .a(H60), .b(H61), .e(H64), .d(H63), .c(H62), .dp(H67));
  BCD_Display bcd_display_2 (.BCD(S2), .SEG({H27, H26, H25, H24, H23, H22, H21, H20}));
  BCD_Display bcd_display_3 (.BCD(SW15_8[3:0]), .SEG({H67, H66, H65, H64, H63, H62, H61, H60}));
  BCD_Adder_2 bcd_adder_2_1 (
    .A1(SW15_8[7:4]), .A0(SW15_8[3:0]), .B1(SW7_0[7:4]), .B0(SW7_0[3:0]), .S0(S0), .S1(S1), .S2(S2),
    .ERROR(ERROR));
  _7_Segment_Display #(.decimalPoint("true")) HEX1 (
    .g(H16), .f(H15), .a(H10), .b(H11), .e(H14), .d(H13), .c(H12), .dp(H17));
  _7_Segment_Display #(.decimalPoint("true")) HEX5 (
    .g(H56), .f(H55), .a(H50), .b(H51), .e(H54), .d(H53), .c(H52), .dp(H57));
  BCD_Display bcd_display_4 (.BCD(S1), .SEG({H17, H16, H15, H14, H13, H12, H11, H10}));
  BCD_Display bcd_display_5 (.BCD(SW7_0[7:4]), .SEG({H57, H56, H55, H54, H53, H52, H51, H50}));
  _7_Segment_Display #(.decimalPoint("true")) HEX0 (
    .g(H06), .f(H05), .a(H00), .b(H01), .e(H04), .d(H03), .c(H02), .dp(H07));
  _7_Segment_Display #(.decimalPoint("true")) HEX4 (
    .g(H46), .f(H45), .a(H40), .b(H41), .e(H44), .d(H43), .c(H42), .dp(H47));
  BCD_Display bcd_display_6 (.BCD(S0), .SEG({H07, H06, H05, H04, H03, H02, H01, H00}));
  BCD_Display bcd_display_7 (.BCD(SW7_0[3:0]), .SEG({H47, H46, H45, H44, H43, H42, H41, H40}));

  // Other names for the same wires on the sheet: A[7:0] = SW15_8; A0[3:0] = SW15_8[3:0]; A1[3:0] = SW15_8[7:4];
  //   B[7:0] = SW7_0; B0[3:0] = SW7_0[3:0]; B1[3:0] = SW7_0[7:4];
  //   HEX0_SEG[7:0] = {H07, H06, H05, H04, H03, H02, H01, H00};
  //   HEX1_SEG[7:0] = {H17, H16, H15, H14, H13, H12, H11, H10};
  //   HEX2_SEG[7:0] = {H27, H26, H25, H24, H23, H22, H21, H20};
  //   HEX4_SEG[7:0] = {H47, H46, H45, H44, H43, H42, H41, H40};
  //   HEX5_SEG[7:0] = {H57, H56, H55, H54, H53, H52, H51, H50};
  //   HEX6_SEG[7:0] = {H67, H66, H65, H64, H63, H62, H61, H60};
  //   HEX7_SEG[7:0] = {H77, H76, H75, H74, H73, H72, H71, H70}

  // Notes on the sheet:
  //   PART V  |  Two-digit BCD addition
  //   Two cascaded Part IV BCD adders.  Inputs are packed BCD: 0x99 means decimal 99.
  //   HEX7  |  A1
  //   SUM  |  Hundreds, tens, units
  //   Example: SW15_8 = 1001 1001 and SW7_0 = 1001 1001 displays 99 + 99 = 198.
  //   HEX2  |  S2
  //   HEX6  |  A0
  //   HEX1  |  S1
  //   HEX5  |  B1
  //   HEX0  |  S0
  //   HEX4  |  B0
endmodule

module Part_VI (
  input  [7:0] SW15_8,
  input  [7:0] SW7_0,
  output [3:0] S0,
  output [3:0] S1,
  output [3:0] S2
);

  wire H00, H01, H02, H03, H04, H05, H06, H07, H10, H11, H12, H13, H14, H15, H16, H17, H20, H21, H22, H23,
       H24, H25, H26, H27, H40, H41, H42, H43, H44, H45, H46, H47, H50, H51, H52, H53, H54, H55, H56, H57,
       H60, H61, H62, H63, H64, H65, H66, H67, H70, H71, H72, H73, H74, H75, H76, H77;

  _7_Segment_Display #(.decimalPoint("true")) HEX7 (
    .g(H76), .f(H75), .a(H70), .b(H71), .e(H74), .d(H73), .c(H72), .dp(H77));
  BCD_Display bcd_display_1 (.BCD(SW15_8[7:4]), .SEG({H77, H76, H75, H74, H73, H72, H71, H70}));
  _7_Segment_Display #(.decimalPoint("true")) HEX2 (
    .g(H26), .f(H25), .a(H20), .b(H21), .e(H24), .d(H23), .c(H22), .dp(H27));
  _7_Segment_Display #(.decimalPoint("true")) HEX6 (
    .g(H66), .f(H65), .a(H60), .b(H61), .e(H64), .d(H63), .c(H62), .dp(H67));
  BCD_Display bcd_display_2 (.BCD(S2), .SEG({H27, H26, H25, H24, H23, H22, H21, H20}));
  BCD_Display bcd_display_3 (.BCD(SW15_8[3:0]), .SEG({H67, H66, H65, H64, H63, H62, H61, H60}));
  Algorithm_BCD_2 algorithm_bcd_2_1 (
    .A1(SW15_8[7:4]), .A0(SW15_8[3:0]), .B1(SW7_0[7:4]), .B0(SW7_0[3:0]), .S0(S0), .S1(S1), .S2(S2));
  _7_Segment_Display #(.decimalPoint("true")) HEX1 (
    .g(H16), .f(H15), .a(H10), .b(H11), .e(H14), .d(H13), .c(H12), .dp(H17));
  _7_Segment_Display #(.decimalPoint("true")) HEX5 (
    .g(H56), .f(H55), .a(H50), .b(H51), .e(H54), .d(H53), .c(H52), .dp(H57));
  BCD_Display bcd_display_4 (.BCD(S1), .SEG({H17, H16, H15, H14, H13, H12, H11, H10}));
  BCD_Display bcd_display_5 (.BCD(SW7_0[7:4]), .SEG({H57, H56, H55, H54, H53, H52, H51, H50}));
  _7_Segment_Display #(.decimalPoint("true")) HEX0 (
    .g(H06), .f(H05), .a(H00), .b(H01), .e(H04), .d(H03), .c(H02), .dp(H07));
  _7_Segment_Display #(.decimalPoint("true")) HEX4 (
    .g(H46), .f(H45), .a(H40), .b(H41), .e(H44), .d(H43), .c(H42), .dp(H47));
  BCD_Display bcd_display_6 (.BCD(S0), .SEG({H07, H06, H05, H04, H03, H02, H01, H00}));
  BCD_Display bcd_display_7 (.BCD(SW7_0[3:0]), .SEG({H47, H46, H45, H44, H43, H42, H41, H40}));

  // Other names for the same wires on the sheet: A[7:0] = SW15_8; A0[3:0] = SW15_8[3:0]; A1[3:0] = SW15_8[7:4];
  //   B[7:0] = SW7_0; B0[3:0] = SW7_0[3:0]; B1[3:0] = SW7_0[7:4];
  //   HEX0_SEG[7:0] = {H07, H06, H05, H04, H03, H02, H01, H00};
  //   HEX1_SEG[7:0] = {H17, H16, H15, H14, H13, H12, H11, H10};
  //   HEX2_SEG[7:0] = {H27, H26, H25, H24, H23, H22, H21, H20};
  //   HEX4_SEG[7:0] = {H47, H46, H45, H44, H43, H42, H41, H40};
  //   HEX5_SEG[7:0] = {H57, H56, H55, H54, H53, H52, H51, H50};
  //   HEX6_SEG[7:0] = {H67, H66, H65, H64, H63, H62, H61, H60};
  //   HEX7_SEG[7:0] = {H77, H76, H75, H74, H73, H72, H71, H70}

  // Notes on the sheet:
  //   PART VI  |  Two-digit BCD addition
  //   Two arithmetic / comparator / mux stages matching the PDF pseudo-code.  Inputs are packed BCD: 0x99 means decimal 99.
  //   HEX7  |  A1
  //   SUM  |  Hundreds, tens, units
  //   Example: SW15_8 = 1001 1001 and SW7_0 = 1001 1001 displays 99 + 99 = 198.
  //   HEX2  |  S2
  //   HEX6  |  A0
  //   HEX1  |  S1
  //   HEX5  |  B1
  //   HEX0  |  S0
  //   HEX4  |  B0
endmodule

module Part_VII (
  input  [5:0] SW5_0,
  output [3:0] D0,
  output [3:0] D1
);

  wire H00, H01, H02, H03, H04, H05, H06, H07, H10, H11, H12, H13, H14, H15, H16, H17;

  BCD_Display bcd_display_1 (.BCD(D1), .SEG({H17, H16, H15, H14, H13, H12, H11, H10}));
  _7_Segment_Display #(.decimalPoint("true")) HEX1 (
    .g(H16), .f(H15), .a(H10), .b(H11), .e(H14), .d(H13), .c(H12), .dp(H17));
  Binary6_BCD binary6_bcd_1 (.V(SW5_0), .D0(D0), .D1(D1));
  BCD_Display bcd_display_2 (.BCD(D0), .SEG({H07, H06, H05, H04, H03, H02, H01, H00}));
  _7_Segment_Display #(.decimalPoint("true")) HEX0 (
    .g(H06), .f(H05), .a(H00), .b(H01), .e(H04), .d(H03), .c(H02), .dp(H07));

  // Other names for the same wires on the sheet: HEX0_SEG[7:0] = {H07, H06, H05, H04, H03, H02, H01, H00};
  //   HEX1_SEG[7:0] = {H17, H16, H15, H14, H13, H12, H11, H10}; V[5:0] = SW5_0

  // Notes on the sheet:
  //   PART VII  |  Six-bit binary to two decimal digits
  //   Poke SW5..0 to try every value from 0 to 63. HEX1 is tens and HEX0 is units.
  //   HEX1  |  D1
  //   HEX0  |  D0
endmodule

module Full_Adder (
  input  a,
  input  b,
  input  cin,
  output s,
  output cout
);

  wire undriven, xor_1_out;

  xor xor_1 (xor_1_out, a, b);
  xor xor_2 (s, undriven, cin);
  Multiplexer #(.width(1), .select(1), .enable("false")) multiplexer_1 (.in0(b), .in1(cin), .out(cout), .sel(undriven));

  // Notes on the sheet:
  //   FULL ADDER  |  Figure 2a
  //   s = a XOR b XOR cin; cout = (a XOR b) ? cin : b. Two XOR gates and one 2:1 mux.
  //   Select 0: propagate b. Select 1: propagate cin.
endmodule

module Ripple_Adder_4 (
  input  [3:0] A,
  input  [3:0] B,
  input  cin,
  output [3:0] S,
  output cout
);

  wire FA0_cout, FA1_cout, FA2_cout;

  Full_Adder FA0 (.a(A[0]), .b(B[0]), .cin(cin), .s(S[0]), .cout(FA0_cout));
  Full_Adder FA1 (.a(A[1]), .b(B[1]), .cin(FA0_cout), .s(S[1]), .cout(FA1_cout));
  Full_Adder FA2 (.a(A[2]), .b(B[2]), .cin(FA1_cout), .s(S[2]), .cout(FA2_cout));
  Full_Adder FA3 (.a(A[3]), .b(B[3]), .cin(FA2_cout), .s(S[3]), .cout(cout));

  // Notes on the sheet:
  //   FOUR-BIT RIPPLE-CARRY ADDER
  //   Four instances of Full_Adder. The carry propagates from bit 0 (left) to bit 3 (right).
  //   Open Full_Adder to inspect its XOR / mux implementation.
endmodule

module BCD_Adder_1 (
  input  [3:0] A,
  input  [3:0] B,
  input  cin,
  output [3:0] S0,
  output S1,
  output [3:0] RAW,
  output C4,
  output ERROR
);

  wire above9, badA, badB, r21;

  Ripple_Adder_4 Binary_sum (.A(A), .B(B), .cin(cin), .S(RAW), .cout(C4));
  or or_1 (r21, RAW[2], RAW[1]);
  and and_1 (above9, RAW[3], r21);
  myComparator A___9 (.v3(A[3]), .v2(A[2]), .v1(A[1]), .v0(A[0]), .z(badA));
  myComparator B___9 (.v3(B[3]), .v2(B[2]), .v1(B[1]), .v0(B[0]), .z(badB));
  or or_2 (S1, C4, above9);
  Ripple_Adder_4 BCD_correction (.A(RAW), .B({1'b0, {2{S1}}, 1'b0}), .cin(1'b0), .S(S0));  // open: cout
  or or_3 (ERROR, badA, badB);

  // Other names for the same wires on the sheet: CORRECTION[2:1] = {2{S1}}; r0 = RAW[0]; r1 = RAW[1]; r2 = RAW[2];
  //   r3 = RAW[3]

  // Notes on the sheet:
  //   ONE-DIGIT BCD ADDER
  //   A + B + cin = 0..19. Add 6 to the raw low nibble when decimal carry k is asserted.
  //   S1 = C4 OR (r3 AND (r2 OR r1)). Invalid BCD inputs assert ERROR; decimal sum is then unspecified.
endmodule

module BCD_Adder_2 (
  input  [3:0] A1,
  input  [3:0] A0,
  input  [3:0] B1,
  input  [3:0] B0,
  output [3:0] S0,
  output [3:0] S1,
  output [3:0] S2,
  output ERROR
);

  wire carry1, e0, e1;

  BCD_Adder_1 Units_digit (.A(A0), .B(B0), .cin(1'b0), .S0(S0), .S1(carry1), .ERROR(e0));  // open: RAW, C4
  BCD_Adder_1 Tens_digit (.A(A1), .B(B1), .cin(carry1), .S0(S1), .S1(S2[0]), .ERROR(e1));  // open: RAW, C4
  or or_1 (ERROR, e0, e1);

  assign S2[3:1] = 3'b000;

  // Other names for the same wires on the sheet: carry2 = S2[0]

  // Notes on the sheet:
  //   TWO-DIGIT BCD ADDER  |  Part V core
  //   Two instances of the Part IV adder. Decimal carry from the units stage feeds the tens stage.
endmodule

module Algorithm_Digit (
  input  [3:0] A,
  input  [3:0] B,
  input  cin,
  output [3:0] S,
  output carry
);

  wire [4:0] T, Z;
  wire [4:4] S5;

  Adder #(.width(5)) adder_1 (.a({1'b0, A}), .b({1'b0, B}), .out(T), .cin(cin));  // open: cout
  Comparator #(.width(5), .mode("unsigned")) comparator_1 (.a(T), .b(5'b01001), .gt(carry));  // open: eq, lt
  Multiplexer #(.width(5), .select(1), .enable("false")) multiplexer_1 (
    .in0({5{1'b0}}), .in1(5'b01010), .out(Z), .sel(carry));
  Subtractor #(.width(5)) subtractor_1 (.a(T), .b(Z), .out({S5[4], S}), .bin(1'b0));  // open: bout

  // Other names for the same wires on the sheet: A5[3:0] = A; B5[3:0] = B; S5[3:0] = S; unused = S5[4]

  // Notes on the sheet:
  //   ALGORITHMIC DECIMAL DIGIT  |  Part VI stage
  //   T = A + B + cin; carry = T > 9; Z = carry ? 10 : 0; S = T - Z.
  //   Five-bit arithmetic preserves the carry at 16..19. All comparators use unsigned mode.
endmodule

module Algorithm_BCD_2 (
  input  [3:0] A1,
  input  [3:0] A0,
  input  [3:0] B1,
  input  [3:0] B0,
  output [3:0] S0,
  output [3:0] S1,
  output [3:0] S2
);

  wire carry1;

  Algorithm_Digit Units__T0___Z0 (.A(A0), .B(B0), .cin(1'b0), .S(S0), .carry(carry1));
  Algorithm_Digit Tens__T1___Z1 (.A(A1), .B(B1), .cin(carry1), .S(S1), .carry(S2[0]));

  assign S2[3:1] = 3'b000;

  // Other names for the same wires on the sheet: carry2 = S2[0]

  // Notes on the sheet:
  //   ALGORITHMIC TWO-DIGIT BCD ADDER
  //   Part VI visual counterpart: two comparator / mux / subtractor stages, with decimal carry between them.
endmodule

module Binary6_BCD (
  input  [5:0] V,
  output [3:0] D0,
  output [3:0] D1
);

  wire [0:0] H1, H2, H3, H4, H5, H6;
  wire [1:0] discard;
  wire [3:0] COUNT1, COUNT2, COUNT3, COUNT4, COUNT5;
  wire [5:0] R1, R2, R3, R4, R5;

  Adder #(.width(4)) adder_1 (.a(4'b0000), .b({3'b000, H1[0]}), .out(COUNT1), .cin(1'b0));  // open: cout
  Adder #(.width(4)) adder_2 (.a(COUNT3), .b({3'b000, H4[0]}), .out(COUNT4), .cin(1'b0));  // open: cout
  Subtract_10_Stage Stage_1 (.V(V), .R(R1), .hit(H1[0]));
  Subtract_10_Stage Stage_4 (.V(R3), .R(R4), .hit(H4[0]));
  Adder #(.width(4)) adder_3 (.a(COUNT1), .b({3'b000, H2[0]}), .out(COUNT2), .cin(1'b0));  // open: cout
  Adder #(.width(4)) adder_4 (.a(COUNT4), .b({3'b000, H5[0]}), .out(COUNT5), .cin(1'b0));  // open: cout
  Subtract_10_Stage Stage_2 (.V(R1), .R(R2), .hit(H2[0]));
  Subtract_10_Stage Stage_5 (.V(R4), .R(R5), .hit(H5[0]));
  Adder #(.width(4)) adder_5 (.a(COUNT2), .b({3'b000, H3[0]}), .out(COUNT3), .cin(1'b0));  // open: cout
  Adder #(.width(4)) adder_6 (.a(COUNT5), .b({3'b000, H6[0]}), .out(D1), .cin(1'b0));  // open: cout
  Subtract_10_Stage Stage_3 (.V(R2), .R(R3), .hit(H3[0]));
  Subtract_10_Stage Stage_6 (.V(R5), .R({discard, D0}), .hit(H6[0]));

  // Other names for the same wires on the sheet: h1_t = H1[0]; h2_t = H2[0]; h3_t = H3[0]; h4_t = H4[0]; h5_t = H5[0];
  //   h6_t = H6[0]; R6[5:0] = {discard, D0}

  // Notes on the sheet:
  //   SIX-BIT BINARY TO BCD  |  Part VII core
  //   Six conditional subtract-10 stages produce a remainder below 10. The number of successful stages is the tens digit.
  //   Input range: 000000 (00) through 111111 (63). All six hit bits are counted; no ROM or lookup table.
endmodule

module Subtract_10_Stage (
  input  [5:0] V,
  output [5:0] R,
  output hit
);

  wire [5:0] MINUS10;

  Comparator #(.width(6), .mode("unsigned")) comparator_1 (.a(V), .b(6'b001001), .gt(hit));  // open: eq, lt
  Subtractor #(.width(6)) subtractor_1 (.a(V), .b(6'b001010), .out(MINUS10), .bin(1'b0));  // open: bout
  Multiplexer #(.width(6), .select(1), .enable("false")) multiplexer_1 (.in0(V), .in1(MINUS10), .out(R), .sel(hit));

  // Notes on the sheet:
  //   CONDITIONAL SUBTRACT-10 STAGE
  //   If V >= 10: R = V - 10 and hit = 1; otherwise R = V and hit = 0. Six-bit unsigned arithmetic.
endmodule

module BCD_Display (
  input  [3:0] BCD,
  output [7:0] SEG
);

  wire [7:0] seg7_decoder_1_o_seg;

  Seg7_Decoder seg7_decoder_1 (
    .i_m3(BCD[3]), .i_m2(BCD[2]), .i_m1(BCD[1]), .i_m0(BCD[0]), .o_seg(seg7_decoder_1_o_seg));
  assign SEG = ~seg7_decoder_1_o_seg;  // NOT_Gate not_1, 8 bits wide

  // Other names for the same wires on the sheet: b0 = BCD[0]; b1 = BCD[1]; b2 = BCD[2]; b3 = BCD[3]

  // Notes on the sheet:
  //   BCD to seven-segment display driver
  //   Reuses the gate-level decoder. SEG[6:0] = g f e d c b a; SEG[7] = decimal point (off).
  //   Invert for Logisim active-high LEDs.
endmodule

module Seg7_Decoder (
  input  i_m3,
  input  i_m2,
  input  i_m1,
  input  i_m0,
  output [7:0] o_seg
);

  wire and_1_out, and_2_out, and_3_out, and_4_out, and_5_out, and_6_out, and_7_out, and_8_out, and_10_out,
       and_11_out, and_12_out, and_13_out, and_14_out, not_1_out, not_2_out, not_3_out, not_4_out;

  not not_1 (not_1_out, i_m3);
  not not_2 (not_2_out, i_m2);
  not not_3 (not_3_out, i_m1);
  not not_4 (not_4_out, i_m0);
  and and_1 (and_1_out, not_1_out, not_2_out, not_3_out);
  and and_2 (and_2_out, i_m2, i_m1, i_m0);
  and and_3 (and_3_out, not_1_out, not_2_out, i_m0);
  and and_4 (and_4_out, not_2_out, i_m1);
  and and_5 (and_5_out, i_m2, not_3_out);
  and and_6 (and_6_out, not_1_out, not_2_out, not_3_out, i_m0);
  and and_7 (and_7_out, i_m2, not_3_out, not_4_out);
  and and_8 (and_8_out, i_m2, i_m1, i_m0);
  and and_9 (o_seg[2], not_2_out, i_m1, not_4_out);
  and and_10 (and_10_out, i_m2, not_3_out, i_m0);
  and and_11 (and_11_out, i_m2, i_m1, not_4_out);
  and and_12 (and_12_out, not_1_out, not_2_out, not_3_out, i_m0);
  and and_13 (and_13_out, i_m2, not_3_out, not_4_out);
  or or_1 (o_seg[6], and_1_out, and_2_out);
  or or_2 (o_seg[5], and_3_out, and_14_out, and_4_out);
  or or_3 (o_seg[4], i_m0, and_5_out);
  or or_4 (o_seg[3], and_6_out, and_7_out, and_8_out);
  or or_5 (o_seg[1], and_10_out, and_11_out);
  or or_6 (o_seg[0], and_12_out, and_13_out);
  and and_14 (and_14_out, i_m1, i_m0);

  assign o_seg[7] = 1'b1;

  // Other names for the same wires on the sheet: fix_v0 = i_m0; fix_v1 = i_m1

  // Notes on the sheet:
  //   Segment f correction
  //   Add v1 AND v0: turns f off for digit 7.
endmodule

module myComparator (
  input  v3,
  input  v2,
  input  v1,
  input  v0,
  output z
);

  wire and_1_out, and_2_out;

  and and_1 (and_1_out, v3, v1);
  and and_2 (and_2_out, v3, v2);
  or or_1 (z, and_1_out, and_2_out);
endmodule

module CircuitA (
  input  i2,
  input  i1,
  input  i0,
  output o2,
  output o1,
  output o0
);

  not not_1 (o1, i1);
  and and_1 (o2, i2, i1);

  assign o0 = i0;
endmodule

module CircuitB (
  input  z,
  output s6,
  output s5,
  output s4,
  output s3,
  output s2,
  output s1,
  output s0
);

  not not_1 (s0, z);

  assign s1 = 1'b1;
  assign s2 = 1'b1;
  assign s3 = s0;
  assign s4 = s0;
  assign s5 = s0;
  assign s6 = 1'b0;
endmodule
