// Logisim project Gated_D_Latch.circ as structural Verilog: 1 circuit, main circuit main
module main (
  input  D,
  input  Clk,
  output Qa_Q,
  output Qb
);

  wire not_1_out, R_g_out, S_g_out;

  not not_1 (not_1_out, D);
  nand S_g (S_g_out, D, Clk);
  nand R_g (R_g_out, Clk, not_1_out);
  nand nand_1 (Qa_Q, S_g_out, Qb);
  nand nand_2 (Qb, Qa_Q, R_g_out);

  // Notes on the sheet:
  //   S
  //   R
endmodule
