// Logisim project Gated_RS_Latch.circ as structural Verilog: 1 circuit, main circuit main
module main (
  input  R,
  input  Clk,
  input  S,
  output Qa_Q,
  output Qb
);

  wire R_g_out, S_g_out;

  and R_g (R_g_out, R, Clk);
  and S_g (S_g_out, Clk, S);
  nor nor_1 (Qa_Q, R_g_out, Qb);
  nor nor_2 (Qb, Qa_Q, S_g_out);
endmodule
