// Logisim project Master_Slave_D_Flip_Flop.circ as structural Verilog: 1 circuit, main circuit main
module main (
  input  D,
  input  Clock,
  output Q,
  output Q_bar
);

  wire Master_qa_q, not_1_out;

  not not_1 (not_1_out, Clock);
  Gated_D_Latch_main Master (.D(D), .Clk(not_1_out), .Qa_Q(Master_qa_q));  // open: Qb
  Gated_D_Latch_main Slave (.D(Master_qa_q), .Clk(Clock), .Qa_Q(Q), .Qb(Q_bar));

  // Notes on the sheet:
  //   Qm
  //   Qs
endmodule
