// Logisim project Storage_Element_Comparison.circ as structural Verilog: 3 circuits, main circuit main
module main (
  input  D,
  input  Clock,
  output Qa,
  output Qa_bar,
  output Qb,
  output Qb_bar,
  output Qc,
  output Qc_bar
);

  Gated_D_Latch_main Gated_D_Latch (.D(D), .Clk(Clock), .Qa_Q(Qa), .Qb(Qa_bar));
  rising_edge_d_flip_flop Rising_edge_D_Flip_Flop (.D(D), .Clk(Clock), .Q(Qb), .Q_bar(Qb_bar));
  falling_edge_d_flip_flop Falling_edge_D_Flip_Flop (.D(D), .Clk(Clock), .Q(Qc), .Q_bar(Qc_bar));
endmodule

module rising_edge_d_flip_flop (
  input  D,
  input  Clk,
  output Q,
  output Q_bar
);

  D_Flip_Flop d_ff_1 (.D(D), .clk(Clk), .Q(Q), .Qn(Q_bar), .preset(1'b0), .reset(1'b0));
endmodule

module falling_edge_d_flip_flop (
  input  D,
  input  Clk,
  output Q,
  output Q_bar
);

  D_Flip_Flop #(.trigger("falling")) d_ff_1 (.D(D), .clk(Clk), .Q(Q), .Qn(Q_bar), .preset(1'b0), .reset(1'b0));
endmodule
